# Fritzing sketch espbutton-schema (saved by Fritzing 0.9.3b)
breadboards: 1

parts:
  U1 = ESP8266 WiFi Module [part_number=ESP8266]
  R1 = Resistor [tolerance=±5% resistance=1k package="0603 [SMD]"]
  R2 = Resistor [tolerance=±5% resistance=1k package="0603 [SMD]"]
  S1 = Toggle Switch [package=THT]
  S2 = Pushbutton [package=THT]
  R3 = Resistor [tolerance=±5% resistance=1k package="0603 [SMD]"]
  Debugger1 = Debugger
  VCC1 = Battery

nets:
  N1: U1.RXD, Debugger1.TX
  N2: U1.VCC, U1.GPIO_2, R2.Pin_1, R3.Pin_0, VCC1.+
  N3: U1.GPIO_0, R2.Pin_0, S1.COM
  N4: U1.CH_PD, R1.Pin_0
  N5: U1.GND, U1.GPIO_15, R1.Pin_1, S1.L2, S2.leg0, VCC1.-
  N6: U1.TXD, Debugger1.GND, Debugger1.RX
  N7: U1.REST, S2.leg1, R3.Pin_1

notes:
  ESP8266 12F
  RST
  EN
  Vcc
  Gpio15
  Gpio2
  Gpio0
  Progr.
  RST button
  Debugger
